// Logisim project bfcpu.circ as structural Verilog: 21 circuits, main circuit main
module main (
  input  in_1,
  input  in_2,
  input  in_3,
  input  in_4,
  input  in_5,
  input  in_6,
  input  in_7,
  input  in_8,
  input  Clock,
  input  En,
  input  Reset,
  input  in_12,
  input  in_13,
  input  in_14,
  input  in_15,
  input  in_16,
  input  in_17,
  input  in_18,
  input  in_19,
  input  in_20,
  input  in_21,
  output [7:0] MP_Out,
  output [7:0] IP_Out,
  output [7:0] Memory_Out
);

  wire and_1_out, or_1_out, undriven, undriven_3, undriven_5, undriven_7;
  wire [7:0] clock_stage_1_out_4, register_module_1_inc_mem, undriven_2, undriven_4, undriven_6;

  Clock_Stage clock_stage_1 (.C(Clock), .En(En), .R(Reset), .out_4(clock_stage_1_out_4));
  RAM_Module ram_module_1 (
    .C(undriven), .I0(in_1), .I1(in_2), .I2(in_3), .I3(in_4), .I4(in_5), .I5(in_6), .I6(in_7), .I7(in_8),
    .O0(in_1), .O1(in_2), .O2(in_3), .O3(in_4), .O4(in_5), .O5(in_6), .O6(in_7), .O7(in_8));  // open: Set_Address_Reg, Bus____Write, Read____Bus
  or or_1 (or_1_out, clock_stage_1_out_4[6], clock_stage_1_out_4[5]);
  and and_1 (and_1_out, or_1_out, Clock);
  Instruction_Module instruction_module_1 (
    .C(and_1_out), .Bus__Reg(clock_stage_1_out_4[6]), .Reg__Bus(clock_stage_1_out_4[5]),
    .BOut({in_8, in_7, in_6, in_5, in_4, in_3, in_2, in_1}),
    .BIn({in_8, in_7, in_6, in_5, in_4, in_3, in_2, in_1}));  // open: Write_Inst, WIn, WAddr
  Register_Module register_module_1 (
    .En(in_12), .C(Clock), .Set_I(in_16), .Set_M(in_15), .Set_IP(in_14), .Set_MP(in_13), .B0(in_1),
    .B1(in_2), .B2(in_3), .B3(in_4), .B4(in_5), .B5(in_6), .B6(in_7), .B7(in_8), .Instruction(in_17),
    .In_to_Mem(register_module_1_inc_mem[7]), .Mem_to_Out(register_module_1_inc_mem[6]),
    .Stack_to_IP(register_module_1_inc_mem[5]), .IP_to_Stack(register_module_1_inc_mem[4]),
    .Dec_MP(register_module_1_inc_mem[3]), .Inc_MP(register_module_1_inc_mem[2]),
    .Dec_Mem(register_module_1_inc_mem[1]), .Inc_Mem(register_module_1_inc_mem[0]), .MP_In(undriven_2),
    .MP_Out(MP_Out), .MP_In_Switch(undriven_3), .IP_In(undriven_4), .IP_Out(IP_Out),
    .IP_In_Switch(undriven_5), .Mem_In(undriven_6), .Mem_Out(Memory_Out), .Mem_In_Switch(undriven_7),
    .IP_to_Bus(in_19), .MP_to_Bus(in_18), .Mem_to_Bus(in_20), .O0(in_1), .O1(in_2), .O2(in_3), .O3(in_4),
    .O4(in_5), .O5(in_6), .O6(in_7), .O7(in_8));
endmodule

module _8b_Register (
  input  Inv,
  input  C,
  input  En,
  input  I1,
  input  I2,
  input  I3,
  input  I4,
  input  I5,
  input  I6,
  input  I7,
  input  I8,
  output O1,
  output O2,
  output O3,
  output O4,
  output O5,
  output O6,
  output O7,
  output O8
);

  wire d_ff_1_q, d_ff_2_q, d_ff_3_q, d_ff_4_q, d_ff_5_q, d_ff_6_q, d_ff_7_q, d_ff_8_q;

  D_Flip_Flop d_ff_1 (.clk(C), .D(I1), .Q(d_ff_1_q), .en(En));  // open: Qn, preset, reset
  D_Flip_Flop d_ff_2 (.clk(C), .D(I2), .Q(d_ff_2_q), .en(En));  // open: Qn, preset, reset
  D_Flip_Flop d_ff_3 (.clk(C), .D(I3), .Q(d_ff_3_q), .en(En));  // open: Qn, preset, reset
  D_Flip_Flop d_ff_4 (.clk(C), .D(I4), .Q(d_ff_4_q), .en(En));  // open: Qn, preset, reset
  D_Flip_Flop d_ff_5 (.clk(C), .D(I5), .Q(d_ff_5_q), .en(En));  // open: Qn, preset, reset
  D_Flip_Flop d_ff_6 (.clk(C), .D(I6), .Q(d_ff_6_q), .en(En));  // open: Qn, preset, reset
  D_Flip_Flop d_ff_7 (.clk(C), .D(I7), .Q(d_ff_7_q), .en(En));  // open: Qn, preset, reset
  D_Flip_Flop d_ff_8 (.clk(C), .D(I8), .Q(d_ff_8_q), .en(En));  // open: Qn, preset, reset
  xor xor_1 (O1, Inv, d_ff_1_q);
  xor xor_2 (O2, Inv, d_ff_2_q);
  xor xor_3 (O3, Inv, d_ff_3_q);
  xor xor_4 (O4, Inv, d_ff_4_q);
  xor xor_5 (O5, Inv, d_ff_5_q);
  xor xor_6 (O6, Inv, d_ff_6_q);
  xor xor_7 (O7, Inv, d_ff_7_q);
  xor xor_8 (O8, Inv, d_ff_8_q);
endmodule

module _4b_Register (
  input  Inv,
  input  En,
  input  C,
  input  I1,
  input  I2,
  input  I3,
  input  I4,
  output O1,
  output O2,
  output O3,
  output O4
);

  wire and_1_out, d_ff_1_q, d_ff_2_q, d_ff_3_q, d_ff_4_q;

  and and_1 (and_1_out, En, C);
  D_Flip_Flop d_ff_1 (.clk(and_1_out), .D(I1), .Q(d_ff_1_q));  // open: Qn, preset, en, reset
  D_Flip_Flop d_ff_2 (.clk(and_1_out), .D(I2), .Q(d_ff_2_q));  // open: Qn, preset, en, reset
  D_Flip_Flop d_ff_3 (.clk(and_1_out), .D(I3), .Q(d_ff_3_q));  // open: Qn, preset, en, reset
  D_Flip_Flop d_ff_4 (.clk(and_1_out), .D(I4), .Q(d_ff_4_q));  // open: Qn, preset, en, reset
  xor xor_1 (O1, Inv, d_ff_1_q);
  xor xor_2 (O2, Inv, d_ff_2_q);
  xor xor_3 (O3, Inv, d_ff_3_q);
  xor xor_4 (O4, Inv, d_ff_4_q);
endmodule

module Inc_Dec_8b (
  input  I_D,
  input  En,
  input  I0,
  input  I1,
  input  I2,
  input  I3,
  input  I4,
  input  I5,
  input  I6,
  input  I7,
  output O0,
  output O1,
  output O2,
  output O3,
  output O4,
  output O5,
  output O6,
  output O7
);

  wire half_adder_1_carryout, half_adder_2_carryout, half_adder_3_carryout, half_adder_4_carryout,
       half_adder_5_carryout, half_adder_6_carryout, half_adder_7_carryout, half_subtracter_1_bout,
       half_subtracter_2_bout, half_subtracter_3_bout, half_subtracter_4_bout, half_subtracter_5_bout,
       half_subtracter_6_bout, half_subtracter_7_bout, not_1_out;
  wire [3:0] half_adder_1_o, half_adder_5_o;
  wire [7:0] demultiplexer_1_out0, demultiplexer_1_out1, half_subtracter_1_dout, multiplexer_1_out;

  Demultiplexer #(.width(8)) demultiplexer_1 (
    .out0(demultiplexer_1_out0), .out1(demultiplexer_1_out1), .in({I7, I6, I5, I4, I3, I2, I1, I0}),
    .sel(I_D), .en(En));
  Half_Adder half_adder_1 (
    .A(demultiplexer_1_out0[0]), .B(1'b1), .CarryIn(1'b0), .CarryOut(half_adder_1_carryout),
    .O(half_adder_1_o[0]));
  Half_Adder half_adder_2 (
    .A(demultiplexer_1_out0[1]), .B(1'b0), .CarryIn(half_adder_1_carryout), .CarryOut(half_adder_2_carryout),
    .O(half_adder_1_o[1]));
  Half_Adder half_adder_3 (
    .A(demultiplexer_1_out0[2]), .B(1'b0), .CarryIn(half_adder_2_carryout), .CarryOut(half_adder_3_carryout),
    .O(half_adder_1_o[2]));
  Half_Adder half_adder_4 (
    .A(demultiplexer_1_out0[3]), .B(1'b0), .CarryIn(half_adder_3_carryout), .CarryOut(half_adder_4_carryout),
    .O(half_adder_1_o[3]));
  Half_Subtracter half_subtracter_1 (
    .Bin(1'b0), .X(demultiplexer_1_out1[0]), .Y(1'b1), .Dout(half_subtracter_1_dout[0]),
    .Bout(half_subtracter_1_bout));
  Half_Subtracter half_subtracter_2 (
    .Bin(half_subtracter_1_bout), .X(demultiplexer_1_out1[1]), .Y(1'b0), .Dout(half_subtracter_1_dout[1]),
    .Bout(half_subtracter_2_bout));
  Half_Subtracter half_subtracter_3 (
    .Bin(half_subtracter_2_bout), .X(demultiplexer_1_out1[2]), .Y(1'b0), .Dout(half_subtracter_1_dout[2]),
    .Bout(half_subtracter_3_bout));
  Half_Subtracter half_subtracter_4 (
    .Bin(half_subtracter_3_bout), .X(demultiplexer_1_out1[3]), .Y(1'b0), .Dout(half_subtracter_1_dout[3]),
    .Bout(half_subtracter_4_bout));
  Half_Subtracter half_subtracter_5 (
    .Bin(half_subtracter_4_bout), .X(demultiplexer_1_out1[4]), .Y(1'b0), .Dout(half_subtracter_1_dout[4]),
    .Bout(half_subtracter_5_bout));
  Half_Subtracter half_subtracter_6 (
    .Bin(half_subtracter_5_bout), .X(demultiplexer_1_out1[5]), .Y(1'b0), .Dout(half_subtracter_1_dout[5]),
    .Bout(half_subtracter_6_bout));
  Half_Subtracter half_subtracter_7 (
    .Bin(half_subtracter_6_bout), .X(demultiplexer_1_out1[6]), .Y(1'b0), .Dout(half_subtracter_1_dout[6]),
    .Bout(half_subtracter_7_bout));
  Half_Subtracter half_subtracter_8 (
    .Bin(half_subtracter_7_bout), .X(demultiplexer_1_out1[7]), .Y(1'b0), .Dout(half_subtracter_1_dout[7]));  // open: Bout
  Half_Adder half_adder_5 (
    .A(demultiplexer_1_out0[4]), .B(1'b0), .CarryIn(half_adder_4_carryout), .CarryOut(half_adder_5_carryout),
    .O(half_adder_5_o[0]));
  Half_Adder half_adder_6 (
    .A(demultiplexer_1_out0[5]), .B(1'b0), .CarryIn(half_adder_5_carryout), .CarryOut(half_adder_6_carryout),
    .O(half_adder_5_o[1]));
  Half_Adder half_adder_7 (
    .A(demultiplexer_1_out0[6]), .B(1'b0), .CarryIn(half_adder_6_carryout), .CarryOut(half_adder_7_carryout),
    .O(half_adder_5_o[2]));
  Half_Adder half_adder_8 (
    .A(demultiplexer_1_out0[7]), .B(1'b0), .CarryIn(half_adder_7_carryout), .O(half_adder_5_o[3]));  // open: CarryOut
  Multiplexer #(.width(8)) multiplexer_1 (
    .in0({half_adder_5_o, half_adder_1_o}), .in1(half_subtracter_1_dout), .out(multiplexer_1_out), .sel(I_D),
    .en(En));
  not not_1 (not_1_out, En);
  Multiplexer #(.width(8), .enable("false")) multiplexer_2 (
    .in0(multiplexer_1_out), .in1({I7, I6, I5, I4, I3, I2, I1, I0}), .out({O7, O6, O5, O4, O3, O2, O1, O0}),
    .sel(not_1_out));
endmodule

module Inc_Dec_4b (
  input  En,
  input  I_D,
  input  I0,
  input  I1,
  input  I2,
  input  I3,
  output O0,
  output O1,
  output O2,
  output O3
);

  wire demultiplexer_1_out0, demultiplexer_1_out1, demultiplexer_2_out0, demultiplexer_2_out1,
       demultiplexer_3_out0, demultiplexer_3_out1, demultiplexer_4_out0, demultiplexer_4_out1,
       half_adder_1_carryout, half_adder_2_carryout, half_adder_3_carryout, half_adder_4_carryout,
       half_subtracter_1_bout, half_subtracter_2_bout, half_subtracter_3_bout;
  wire [3:0] half_adder_1_o, half_subtracter_1_dout;

  Demultiplexer demultiplexer_1 (.out0(demultiplexer_1_out0), .out1(demultiplexer_1_out1), .in(I0), .sel(I_D), .en(En));
  Demultiplexer demultiplexer_2 (.out0(demultiplexer_2_out0), .out1(demultiplexer_2_out1), .in(I1), .sel(I_D), .en(En));
  Demultiplexer demultiplexer_3 (.out0(demultiplexer_3_out0), .out1(demultiplexer_3_out1), .in(I2), .sel(I_D), .en(En));
  Demultiplexer demultiplexer_4 (.out0(demultiplexer_4_out0), .out1(demultiplexer_4_out1), .in(I3), .sel(I_D), .en(En));
  Half_Subtracter half_subtracter_1 (
    .Bin(1'b0), .X(demultiplexer_1_out1), .Y(1'b1), .Dout(half_subtracter_1_dout[0]),
    .Bout(half_subtracter_1_bout));
  Half_Subtracter half_subtracter_2 (
    .Bin(half_subtracter_1_bout), .X(demultiplexer_2_out1), .Y(1'b0), .Dout(half_subtracter_1_dout[1]),
    .Bout(half_subtracter_2_bout));
  Half_Subtracter half_subtracter_3 (
    .Bin(half_subtracter_2_bout), .X(demultiplexer_3_out1), .Y(1'b0), .Dout(half_subtracter_1_dout[2]),
    .Bout(half_subtracter_3_bout));
  Half_Subtracter half_subtracter_4 (
    .Bin(half_subtracter_3_bout), .X(demultiplexer_4_out1), .Y(1'b0), .Dout(half_subtracter_1_dout[3]));  // open: Bout
  Half_Adder half_adder_1 (
    .A(1'b1), .B(demultiplexer_1_out0), .CarryIn(1'b0), .CarryOut(half_adder_1_carryout),
    .O(half_adder_1_o[0]));
  Half_Adder half_adder_2 (
    .A(1'b0), .B(demultiplexer_2_out0), .CarryIn(half_adder_1_carryout), .CarryOut(half_adder_2_carryout),
    .O(half_adder_1_o[1]));
  Half_Adder half_adder_3 (
    .A(1'b0), .B(demultiplexer_3_out0), .CarryIn(half_adder_2_carryout), .CarryOut(half_adder_3_carryout),
    .O(half_adder_1_o[2]));
  Half_Adder half_adder_4 (
    .A(1'b0), .B(demultiplexer_4_out0), .CarryIn(half_adder_3_carryout), .CarryOut(half_adder_4_carryout),
    .O(half_adder_1_o[3]));
  Multiplexer #(.width(4), .disabled(0)) multiplexer_1 (
    .in0(half_adder_1_o), .in1(half_subtracter_1_dout), .out({O3, O2, O1, O0}), .sel(I_D), .en(En));

  // Notes on the sheet:
  //   Decrement
  //   Increment
endmodule

module Half_Adder (
  input  CarryIn,
  input  A,
  input  B,
  output O,
  output CarryOut
);

  wire and_1_out, and_2_out, xor_1_out;

  xor xor_1 (xor_1_out, A, B);
  xor xor_2 (O, CarryIn, xor_1_out);
  and and_1 (and_1_out, CarryIn, xor_1_out);
  and and_2 (and_2_out, A, B);
  or or_1 (CarryOut, and_1_out, and_2_out);
endmodule

module Half_Subtracter (
  input  Bin,
  input  X,
  input  Y,
  output Dout,
  output Bout
);

  wire and_1_out, and_2_out, not_1_out, not_2_out, xor_1_out;

  not not_1 (not_1_out, X);
  xor xor_1 (xor_1_out, X, Y);
  and and_1 (and_1_out, not_1_out, Y);
  xor xor_2 (Dout, Bin, xor_1_out);
  not not_2 (not_2_out, xor_1_out);
  and and_2 (and_2_out, not_2_out, Bin);
  or or_1 (Bout, and_2_out, and_1_out);
endmodule

module Add_Subtract_Abstractor (
  input  En,
  input  Inc,
  input  Dec,
  input  [7:0] Input,
  output Write_Enable__Out,
  output [7:0] Output
);

  wire and_1_out, not_1_out, or_1_out;

  not not_1 (not_1_out, Inc);
  or or_1 (or_1_out, Inc, Dec);
  and and_1 (and_1_out, not_1_out, Dec);
  and and_2 (Write_Enable__Out, En, or_1_out);
  Inc_Dec_8b inc_dec_8b_1 (
    .I_D(and_1_out), .En(Write_Enable__Out), .I0(Input[0]), .I1(Input[1]), .I2(Input[2]), .I3(Input[3]),
    .I4(Input[4]), .I5(Input[5]), .I6(Input[6]), .I7(Input[7]), .O0(Output[0]), .O1(Output[1]),
    .O2(Output[2]), .O3(Output[3]), .O4(Output[4]), .O5(Output[5]), .O6(Output[6]), .O7(Output[7]));
endmodule

module _2b_Selector (
  input  En,
  input  S0,
  input  S1,
  input  S2,
  input  S3,
  output O0,
  output O1
);

  wire or_1_out, or_2_out;

  or or_1 (or_1_out, S2, S3);
  or or_2 (or_2_out, S1, S3);
  Multiplexer multiplexer_1 (.in0(or_1_out), .out(O0), .sel(1'b0), .en(En));  // open: in1
  Multiplexer multiplexer_2 (.in0(or_2_out), .out(O1), .sel(1'b0), .en(En));  // open: in1
endmodule

module _16b_memory (
  input  WEn,
  input  WEn_2,
  input  En,
  input  En_2,
  input  C,
  input  [3:0] Address,
  input  [7:0] In,
  output [7:0] Out
);

  wire and_1_out, and_2_out;

  Stack_Storage stack_storage_1 (
    .C(C), .R0(Address[3]), .R1(Address[2]), .R2(Address[1]), .R3(Address[0]), .En(and_2_out),
    .WEn(and_1_out), .I7(In[7]), .I6(In[6]), .I5(In[5]), .I4(In[4]), .I3(In[3]), .I2(In[2]), .I1(In[1]),
    .I0(In[0]), .O7(Out[7]), .O6(Out[6]), .O5(Out[5]), .O4(Out[4]), .O3(Out[3]), .O2(Out[2]), .O1(Out[1]),
    .O0(Out[0]));
  and and_1 (and_1_out, WEn, WEn_2);
  and and_2 (and_2_out, En, En_2);
endmodule

module _256B_Memory (
  input  C,
  input  [7:0] WIn,
  input  [7:0] Address,
  input  En,
  input  WEn,
  output [7:0] Bus_Out
);

  wire decoder_1_out0, decoder_1_out1, decoder_1_out2, decoder_1_out3, decoder_2_out0, decoder_2_out1,
       decoder_2_out2, decoder_2_out3, decoder_3_out0, decoder_3_out1, decoder_3_out2, decoder_3_out3,
       decoder_4_out0, decoder_4_out1, decoder_4_out2, decoder_4_out3, n4x_and_1_o0, n4x_and_1_o1,
       n4x_and_1_o2, n4x_and_1_o3, n4x_and_2_o0, n4x_and_2_o1, n4x_and_2_o2, n4x_and_2_o3, n4x_and_3_o0,
       n4x_and_3_o1, n4x_and_3_o2, n4x_and_3_o3, n4x_and_4_o0, n4x_and_4_o1, n4x_and_4_o2, n4x_and_4_o3;
  wire [1:0] n4b_splitter_1_out__0_1, n4b_splitter_1_out__2_3;
  wire [3:0] n8b_splitter_1_out__0_3, n8b_splitter_1_out__4_7;
  wire [7:0] n16b_memory_1_out, n16b_memory_2_out, n16b_memory_3_out, n16b_memory_4_out, n16b_memory_5_out,
       n16b_memory_6_out, n16b_memory_7_out, n16b_memory_8_out, n16b_memory_9_out, n16b_memory_10_out,
       n16b_memory_11_out, n16b_memory_12_out, n16b_memory_13_out, n16b_memory_14_out, n16b_memory_15_out,
       n16b_memory_16_out;

  _4b_Splitter u_4b_splitter_1 (
    .In(n8b_splitter_1_out__0_3), .Out__0_1(n4b_splitter_1_out__0_1), .Out__2_3(n4b_splitter_1_out__2_3));
  _8b_Splitter u_8b_splitter_1 (.In(Address), .Out__0_3(n8b_splitter_1_out__0_3), .Out__4_7(n8b_splitter_1_out__4_7));
  _4x_AND u_4x_and_1 (
    .EN(WEn), .I0(decoder_1_out3), .I1(decoder_1_out2), .I2(decoder_1_out1), .I3(decoder_1_out0),
    .O0(n4x_and_1_o0), .O1(n4x_and_1_o1), .O2(n4x_and_1_o2), .O3(n4x_and_1_o3));
  Decoder #(.select(2)) decoder_1 (
    .out0(decoder_1_out0), .out1(decoder_1_out1), .out2(decoder_1_out2), .out3(decoder_1_out3),
    .sel(n4b_splitter_1_out__0_1));  // open: en
  _4x_AND u_4x_and_2 (
    .EN(En), .I0(decoder_2_out3), .I1(decoder_2_out2), .I2(decoder_2_out1), .I3(decoder_2_out0),
    .O0(n4x_and_2_o0), .O1(n4x_and_2_o1), .O2(n4x_and_2_o2), .O3(n4x_and_2_o3));
  Decoder #(.select(2)) decoder_2 (
    .out0(decoder_2_out0), .out1(decoder_2_out1), .out2(decoder_2_out2), .out3(decoder_2_out3),
    .sel(n4b_splitter_1_out__0_1));  // open: en
  Decoder #(.select(2)) decoder_3 (
    .out0(decoder_3_out0), .out1(decoder_3_out1), .out2(decoder_3_out2), .out3(decoder_3_out3),
    .sel(n4b_splitter_1_out__2_3));  // open: en
  _4x_AND u_4x_and_3 (
    .EN(WEn), .I0(decoder_3_out0), .I1(decoder_3_out1), .I2(decoder_3_out2), .I3(decoder_3_out3),
    .O0(n4x_and_3_o0), .O1(n4x_and_3_o1), .O2(n4x_and_3_o2), .O3(n4x_and_3_o3));
  Decoder #(.select(2)) decoder_4 (
    .out0(decoder_4_out0), .out1(decoder_4_out1), .out2(decoder_4_out2), .out3(decoder_4_out3),
    .sel(n4b_splitter_1_out__2_3));  // open: en
  _4x_AND u_4x_and_4 (
    .EN(En), .I0(decoder_4_out0), .I1(decoder_4_out1), .I2(decoder_4_out2), .I3(decoder_4_out3),
    .O0(n4x_and_4_o0), .O1(n4x_and_4_o1), .O2(n4x_and_4_o2), .O3(n4x_and_4_o3));
  _16b_memory u_16b_memory_1 (
    .WEn_2(n4x_and_3_o0), .En(n4x_and_2_o3), .C(C), .Address(n8b_splitter_1_out__4_7), .In(WIn),
    .Out(n16b_memory_1_out), .WEn(n4x_and_1_o3), .En_2(n4x_and_4_o0));
  _16b_memory u_16b_memory_2 (
    .WEn_2(n4x_and_3_o0), .En(n4x_and_2_o2), .C(C), .Address(n8b_splitter_1_out__4_7), .In(WIn),
    .Out(n16b_memory_2_out), .WEn(n4x_and_1_o2), .En_2(n4x_and_4_o0));
  _16b_memory u_16b_memory_3 (
    .WEn_2(n4x_and_3_o0), .En(n4x_and_2_o1), .C(C), .Address(n8b_splitter_1_out__4_7), .In(WIn),
    .Out(n16b_memory_3_out), .WEn(n4x_and_1_o1), .En_2(n4x_and_4_o0));
  _16b_memory u_16b_memory_4 (
    .WEn_2(n4x_and_3_o0), .En(n4x_and_2_o0), .C(C), .Address(n8b_splitter_1_out__4_7), .In(WIn),
    .Out(n16b_memory_4_out), .WEn(n4x_and_1_o0), .En_2(n4x_and_4_o0));
  _16b_memory u_16b_memory_5 (
    .WEn_2(n4x_and_3_o1), .En(n4x_and_2_o3), .C(C), .Address(n8b_splitter_1_out__4_7), .In(WIn),
    .Out(n16b_memory_5_out), .WEn(n4x_and_1_o3), .En_2(n4x_and_4_o1));
  _16b_memory u_16b_memory_6 (
    .WEn_2(n4x_and_3_o1), .En(n4x_and_2_o2), .C(C), .Address(n8b_splitter_1_out__4_7), .In(WIn),
    .Out(n16b_memory_6_out), .WEn(n4x_and_1_o2), .En_2(n4x_and_4_o1));
  _16b_memory u_16b_memory_7 (
    .WEn_2(n4x_and_3_o1), .En(n4x_and_2_o1), .C(C), .Address(n8b_splitter_1_out__4_7), .In(WIn),
    .Out(n16b_memory_7_out), .WEn(n4x_and_1_o1), .En_2(n4x_and_4_o1));
  _16b_memory u_16b_memory_8 (
    .WEn_2(n4x_and_3_o1), .En(n4x_and_2_o0), .C(C), .Address(n8b_splitter_1_out__4_7), .In(WIn),
    .Out(n16b_memory_8_out), .WEn(n4x_and_1_o0), .En_2(n4x_and_4_o1));
  _16b_memory u_16b_memory_9 (
    .WEn_2(n4x_and_3_o2), .En(n4x_and_2_o3), .C(C), .Address(n8b_splitter_1_out__4_7), .In(WIn),
    .Out(n16b_memory_9_out), .WEn(n4x_and_1_o3), .En_2(n4x_and_4_o2));
  _16b_memory u_16b_memory_10 (
    .WEn_2(n4x_and_3_o2), .En(n4x_and_2_o2), .C(C), .Address(n8b_splitter_1_out__4_7), .In(WIn),
    .Out(n16b_memory_10_out), .WEn(n4x_and_1_o2), .En_2(n4x_and_4_o2));
  _16b_memory u_16b_memory_11 (
    .WEn_2(n4x_and_3_o2), .En(n4x_and_2_o1), .C(C), .Address(n8b_splitter_1_out__4_7), .In(WIn),
    .Out(n16b_memory_11_out), .WEn(n4x_and_1_o1), .En_2(n4x_and_4_o2));
  _16b_memory u_16b_memory_12 (
    .WEn_2(n4x_and_3_o2), .En(n4x_and_2_o0), .C(C), .Address(n8b_splitter_1_out__4_7), .In(WIn),
    .Out(n16b_memory_12_out), .WEn(n4x_and_1_o0), .En_2(n4x_and_4_o2));
  _16b_memory u_16b_memory_13 (
    .WEn_2(n4x_and_3_o3), .En(n4x_and_2_o3), .C(C), .Address(n8b_splitter_1_out__4_7), .In(WIn),
    .Out(n16b_memory_13_out), .WEn(n4x_and_1_o3), .En_2(n4x_and_4_o3));
  _16b_memory u_16b_memory_14 (
    .WEn_2(n4x_and_3_o3), .En(n4x_and_2_o2), .C(C), .Address(n8b_splitter_1_out__4_7), .In(WIn),
    .Out(n16b_memory_14_out), .WEn(n4x_and_1_o2), .En_2(n4x_and_4_o3));
  _16b_memory u_16b_memory_15 (
    .WEn_2(n4x_and_3_o3), .En(n4x_and_2_o1), .C(C), .Address(n8b_splitter_1_out__4_7), .In(WIn),
    .Out(n16b_memory_15_out), .WEn(n4x_and_1_o1), .En_2(n4x_and_4_o3));
  _16b_memory u_16b_memory_16 (
    .WEn_2(n4x_and_3_o3), .En(n4x_and_2_o0), .C(C), .Address(n8b_splitter_1_out__4_7), .In(WIn),
    .Out(n16b_memory_16_out), .WEn(n4x_and_1_o0), .En_2(n4x_and_4_o3));
  Multiplexer #(.select(4), .width(8)) multiplexer_1 (
    .in0(n16b_memory_1_out), .in1(n16b_memory_2_out), .in2(n16b_memory_3_out), .in3(n16b_memory_4_out),
    .in4(n16b_memory_5_out), .in5(n16b_memory_6_out), .in6(n16b_memory_7_out), .in7(n16b_memory_8_out),
    .in8(n16b_memory_9_out), .in9(n16b_memory_10_out), .in10(n16b_memory_11_out), .in11(n16b_memory_12_out),
    .in12(n16b_memory_13_out), .in13(n16b_memory_14_out), .in14(n16b_memory_15_out),
    .in15(n16b_memory_16_out), .out(Bus_Out), .sel(n8b_splitter_1_out__0_3));  // open: en
endmodule

module OR_Matrix_4x4 (
  input  A0,
  input  A1,
  input  A2,
  input  A3,
  input  B0,
  input  B1,
  input  B2,
  input  B3,
  output O0,
  output O1,
  output O2,
  output O3
);

  or or_1 (O0, A0, B0);
  or or_2 (O1, A1, B1);
  or or_3 (O2, A2, B2);
  or or_4 (O3, A3, B3);
endmodule

module _8b_Splitter (
  input  [7:0] In,
  output [3:0] Out__0_3,
  output [3:0] Out__4_7
);


  assign Out__0_3 = In[3:0];
  assign Out__4_7 = In[7:4];
endmodule

module _4b_Splitter (
  input  [3:0] In,
  output [1:0] Out__0_1,
  output [1:0] Out__2_3
);


  assign Out__0_1 = In[1:0];
  assign Out__2_3 = In[3:2];
endmodule

module _4x_AND (
  input  EN,
  input  I0,
  input  I1,
  input  I2,
  input  I3,
  output O0,
  output O1,
  output O2,
  output O3
);

  and and_1 (O0, EN, I0);
  and and_2 (O2, EN, I2);
  and and_3 (O1, EN, I1);
  and and_4 (O3, EN, I3);
endmodule

module Stack (
  input  C,
  input  Add_Pop,
  input  En,
  input  WEn,
  input  I0,
  input  I1,
  input  RegEn,
  input  I2,
  input  I3,
  input  I4,
  input  I5,
  input  I6,
  input  I7,
  input  OEn,
  output O0,
  output O1,
  output O2,
  output O3,
  output O4,
  output O5,
  output O6,
  output O7
);

  wire and_1_out, inc_dec_4b_1_o0, inc_dec_4b_1_o1, inc_dec_4b_1_o2, inc_dec_4b_1_o3, not_1_out, not_2_out;
  wire [3:0] n4b_register_1_o1;
  wire [7:0] stack_storage_1_o0;

  Inc_Dec_4b inc_dec_4b_1 (
    .En(RegEn), .I_D(Add_Pop), .I0(n4b_register_1_o1[0]), .I1(n4b_register_1_o1[1]),
    .I2(n4b_register_1_o1[2]), .I3(n4b_register_1_o1[3]), .O0(inc_dec_4b_1_o0), .O1(inc_dec_4b_1_o1),
    .O2(inc_dec_4b_1_o2), .O3(inc_dec_4b_1_o3));
  _4b_Register u_4b_register_1 (
    .Inv(1'b0), .C(C), .I1(inc_dec_4b_1_o0), .I2(inc_dec_4b_1_o1), .I3(inc_dec_4b_1_o2),
    .I4(inc_dec_4b_1_o3), .O1(n4b_register_1_o1[0]), .O2(n4b_register_1_o1[1]), .O3(n4b_register_1_o1[2]),
    .O4(n4b_register_1_o1[3]), .En(RegEn));
  not not_1 (not_1_out, C);
  not not_2 (not_2_out, Add_Pop);
  Stack_Storage stack_storage_1 (
    .C(not_1_out), .R0(n4b_register_1_o1[0]), .R1(n4b_register_1_o1[1]), .R2(n4b_register_1_o1[2]),
    .R3(n4b_register_1_o1[3]), .En(En), .WEn(and_1_out), .I7(I7), .I6(I6), .I5(I5), .I4(I4), .I3(I3),
    .I2(I2), .I1(I1), .I0(I0), .O7(stack_storage_1_o0[7]), .O6(stack_storage_1_o0[6]),
    .O5(stack_storage_1_o0[5]), .O4(stack_storage_1_o0[4]), .O3(stack_storage_1_o0[3]),
    .O2(stack_storage_1_o0[2]), .O1(stack_storage_1_o0[1]), .O0(stack_storage_1_o0[0]));
  and and_1 (and_1_out, WEn, not_2_out);
  Multiplexer #(.width(8), .enable("false")) multiplexer_1 (
    .in1(stack_storage_1_o0), .out({O7, O6, O5, O4, O3, O2, O1, O0}), .sel(OEn));  // open: in0
endmodule

module Stack_Storage (
  input  C,
  input  R0,
  input  R1,
  input  R2,
  input  R3,
  input  En,
  input  WEn,
  input  I7,
  input  I6,
  input  I5,
  input  I4,
  input  I3,
  input  I2,
  input  I1,
  input  I0,
  output O7,
  output O6,
  output O5,
  output O4,
  output O3,
  output O2,
  output O1,
  output O0
);

  wire demultiplexer_2_out0, demultiplexer_2_out1, demultiplexer_2_out2, demultiplexer_2_out3,
       demultiplexer_2_out4, demultiplexer_2_out5, demultiplexer_2_out6, demultiplexer_2_out7,
       demultiplexer_2_out8, demultiplexer_2_out9, demultiplexer_2_out10, demultiplexer_2_out11,
       demultiplexer_2_out12, demultiplexer_2_out13, demultiplexer_2_out14, demultiplexer_2_out15,
       demultiplexer_3_out0, demultiplexer_3_out1, demultiplexer_3_out2, demultiplexer_3_out3,
       demultiplexer_3_out4, demultiplexer_3_out5, demultiplexer_3_out6, demultiplexer_3_out7,
       demultiplexer_3_out8, demultiplexer_3_out9, demultiplexer_3_out10, demultiplexer_3_out11,
       demultiplexer_3_out12, demultiplexer_3_out13, demultiplexer_3_out14, demultiplexer_3_out15;
  wire [7:0] demultiplexer_1_out0, demultiplexer_1_out1, demultiplexer_1_out2, demultiplexer_1_out3,
       demultiplexer_1_out4, demultiplexer_1_out5, demultiplexer_1_out6, demultiplexer_1_out7,
       demultiplexer_1_out8, demultiplexer_1_out9, demultiplexer_1_out10, demultiplexer_1_out11,
       demultiplexer_1_out12, demultiplexer_1_out13, demultiplexer_1_out14, demultiplexer_1_out15,
       n8b_register_1_o1, n8b_register_2_o1, n8b_register_3_o1, n8b_register_4_o1, n8b_register_5_o1,
       n8b_register_6_o1, n8b_register_7_o1, n8b_register_8_o1, n8b_register_9_o1, n8b_register_10_o1,
       n8b_register_11_o1, n8b_register_12_o1, n8b_register_13_o1, n8b_register_14_o1, n8b_register_15_o1,
       n8b_register_16_o1;

  Demultiplexer #(.select(4), .width(8)) demultiplexer_1 (
    .out0(demultiplexer_1_out0), .out1(demultiplexer_1_out1), .out2(demultiplexer_1_out2),
    .out3(demultiplexer_1_out3), .out4(demultiplexer_1_out4), .out5(demultiplexer_1_out5),
    .out6(demultiplexer_1_out6), .out7(demultiplexer_1_out7), .out8(demultiplexer_1_out8),
    .out9(demultiplexer_1_out9), .out10(demultiplexer_1_out10), .out11(demultiplexer_1_out11),
    .out12(demultiplexer_1_out12), .out13(demultiplexer_1_out13), .out14(demultiplexer_1_out14),
    .out15(demultiplexer_1_out15), .in({I7, I6, I5, I4, I3, I2, I1, I0}), .sel({R3, R2, R1, R0}), .en(En));
  Demultiplexer #(.select(4)) demultiplexer_2 (
    .out0(demultiplexer_2_out0), .out1(demultiplexer_2_out1), .out2(demultiplexer_2_out2),
    .out3(demultiplexer_2_out3), .out4(demultiplexer_2_out4), .out5(demultiplexer_2_out5),
    .out6(demultiplexer_2_out6), .out7(demultiplexer_2_out7), .out8(demultiplexer_2_out8),
    .out9(demultiplexer_2_out9), .out10(demultiplexer_2_out10), .out11(demultiplexer_2_out11),
    .out12(demultiplexer_2_out12), .out13(demultiplexer_2_out13), .out14(demultiplexer_2_out14),
    .out15(demultiplexer_2_out15), .in(C), .sel({R3, R2, R1, R0}), .en(En));
  Demultiplexer #(.select(4)) demultiplexer_3 (
    .out0(demultiplexer_3_out0), .out1(demultiplexer_3_out1), .out2(demultiplexer_3_out2),
    .out3(demultiplexer_3_out3), .out4(demultiplexer_3_out4), .out5(demultiplexer_3_out5),
    .out6(demultiplexer_3_out6), .out7(demultiplexer_3_out7), .out8(demultiplexer_3_out8),
    .out9(demultiplexer_3_out9), .out10(demultiplexer_3_out10), .out11(demultiplexer_3_out11),
    .out12(demultiplexer_3_out12), .out13(demultiplexer_3_out13), .out14(demultiplexer_3_out14),
    .out15(demultiplexer_3_out15), .in(WEn), .sel({R3, R2, R1, R0}), .en(En));
  _8b_Register u_8b_register_1 (
    .Inv(1'b0), .C(demultiplexer_2_out0), .I1(demultiplexer_1_out0[0]), .I2(demultiplexer_1_out0[1]),
    .I3(demultiplexer_1_out0[2]), .I4(demultiplexer_1_out0[3]), .I5(demultiplexer_1_out0[4]),
    .I6(demultiplexer_1_out0[5]), .I7(demultiplexer_1_out0[6]), .I8(demultiplexer_1_out0[7]),
    .O1(n8b_register_1_o1[0]), .O2(n8b_register_1_o1[1]), .O3(n8b_register_1_o1[2]),
    .O4(n8b_register_1_o1[3]), .O5(n8b_register_1_o1[4]), .O6(n8b_register_1_o1[5]),
    .O7(n8b_register_1_o1[6]), .O8(n8b_register_1_o1[7]), .En(demultiplexer_3_out0));
  _8b_Register u_8b_register_2 (
    .Inv(1'b0), .C(demultiplexer_2_out4), .I1(demultiplexer_1_out4[0]), .I2(demultiplexer_1_out4[1]),
    .I3(demultiplexer_1_out4[2]), .I4(demultiplexer_1_out4[3]), .I5(demultiplexer_1_out4[4]),
    .I6(demultiplexer_1_out4[5]), .I7(demultiplexer_1_out4[6]), .I8(demultiplexer_1_out4[7]),
    .O1(n8b_register_2_o1[0]), .O2(n8b_register_2_o1[1]), .O3(n8b_register_2_o1[2]),
    .O4(n8b_register_2_o1[3]), .O5(n8b_register_2_o1[4]), .O6(n8b_register_2_o1[5]),
    .O7(n8b_register_2_o1[6]), .O8(n8b_register_2_o1[7]), .En(demultiplexer_3_out4));
  _8b_Register u_8b_register_3 (
    .Inv(1'b0), .C(demultiplexer_2_out8), .I1(demultiplexer_1_out8[0]), .I2(demultiplexer_1_out8[1]),
    .I3(demultiplexer_1_out8[2]), .I4(demultiplexer_1_out8[3]), .I5(demultiplexer_1_out8[4]),
    .I6(demultiplexer_1_out8[5]), .I7(demultiplexer_1_out8[6]), .I8(demultiplexer_1_out8[7]),
    .O1(n8b_register_3_o1[0]), .O2(n8b_register_3_o1[1]), .O3(n8b_register_3_o1[2]),
    .O4(n8b_register_3_o1[3]), .O5(n8b_register_3_o1[4]), .O6(n8b_register_3_o1[5]),
    .O7(n8b_register_3_o1[6]), .O8(n8b_register_3_o1[7]), .En(demultiplexer_3_out8));
  _8b_Register u_8b_register_4 (
    .Inv(1'b0), .C(demultiplexer_2_out12), .I1(demultiplexer_1_out12[0]), .I2(demultiplexer_1_out12[1]),
    .I3(demultiplexer_1_out12[2]), .I4(demultiplexer_1_out12[3]), .I5(demultiplexer_1_out12[4]),
    .I6(demultiplexer_1_out12[5]), .I7(demultiplexer_1_out12[6]), .I8(demultiplexer_1_out12[7]),
    .O1(n8b_register_4_o1[0]), .O2(n8b_register_4_o1[1]), .O3(n8b_register_4_o1[2]),
    .O4(n8b_register_4_o1[3]), .O5(n8b_register_4_o1[4]), .O6(n8b_register_4_o1[5]),
    .O7(n8b_register_4_o1[6]), .O8(n8b_register_4_o1[7]), .En(demultiplexer_3_out12));
  _8b_Register u_8b_register_5 (
    .Inv(1'b0), .C(demultiplexer_2_out1), .I1(demultiplexer_1_out1[0]), .I2(demultiplexer_1_out1[1]),
    .I3(demultiplexer_1_out1[2]), .I4(demultiplexer_1_out1[3]), .I5(demultiplexer_1_out1[4]),
    .I6(demultiplexer_1_out1[5]), .I7(demultiplexer_1_out1[6]), .I8(demultiplexer_1_out1[7]),
    .O1(n8b_register_5_o1[0]), .O2(n8b_register_5_o1[1]), .O3(n8b_register_5_o1[2]),
    .O4(n8b_register_5_o1[3]), .O5(n8b_register_5_o1[4]), .O6(n8b_register_5_o1[5]),
    .O7(n8b_register_5_o1[6]), .O8(n8b_register_5_o1[7]), .En(demultiplexer_3_out1));
  _8b_Register u_8b_register_6 (
    .Inv(1'b0), .C(demultiplexer_2_out5), .I1(demultiplexer_1_out5[0]), .I2(demultiplexer_1_out5[1]),
    .I3(demultiplexer_1_out5[2]), .I4(demultiplexer_1_out5[3]), .I5(demultiplexer_1_out5[4]),
    .I6(demultiplexer_1_out5[5]), .I7(demultiplexer_1_out5[6]), .I8(demultiplexer_1_out5[7]),
    .O1(n8b_register_6_o1[0]), .O2(n8b_register_6_o1[1]), .O3(n8b_register_6_o1[2]),
    .O4(n8b_register_6_o1[3]), .O5(n8b_register_6_o1[4]), .O6(n8b_register_6_o1[5]),
    .O7(n8b_register_6_o1[6]), .O8(n8b_register_6_o1[7]), .En(demultiplexer_3_out5));
  _8b_Register u_8b_register_7 (
    .Inv(1'b0), .C(demultiplexer_2_out9), .I1(demultiplexer_1_out9[0]), .I2(demultiplexer_1_out9[1]),
    .I3(demultiplexer_1_out9[2]), .I4(demultiplexer_1_out9[3]), .I5(demultiplexer_1_out9[4]),
    .I6(demultiplexer_1_out9[5]), .I7(demultiplexer_1_out9[6]), .I8(demultiplexer_1_out9[7]),
    .O1(n8b_register_7_o1[0]), .O2(n8b_register_7_o1[1]), .O3(n8b_register_7_o1[2]),
    .O4(n8b_register_7_o1[3]), .O5(n8b_register_7_o1[4]), .O6(n8b_register_7_o1[5]),
    .O7(n8b_register_7_o1[6]), .O8(n8b_register_7_o1[7]), .En(demultiplexer_3_out9));
  _8b_Register u_8b_register_8 (
    .Inv(1'b0), .C(demultiplexer_2_out13), .I1(demultiplexer_1_out13[0]), .I2(demultiplexer_1_out13[1]),
    .I3(demultiplexer_1_out13[2]), .I4(demultiplexer_1_out13[3]), .I5(demultiplexer_1_out13[4]),
    .I6(demultiplexer_1_out13[5]), .I7(demultiplexer_1_out13[6]), .I8(demultiplexer_1_out13[7]),
    .O1(n8b_register_8_o1[0]), .O2(n8b_register_8_o1[1]), .O3(n8b_register_8_o1[2]),
    .O4(n8b_register_8_o1[3]), .O5(n8b_register_8_o1[4]), .O6(n8b_register_8_o1[5]),
    .O7(n8b_register_8_o1[6]), .O8(n8b_register_8_o1[7]), .En(demultiplexer_3_out13));
  _8b_Register u_8b_register_9 (
    .Inv(1'b0), .C(demultiplexer_2_out2), .I1(demultiplexer_1_out2[0]), .I2(demultiplexer_1_out2[1]),
    .I3(demultiplexer_1_out2[2]), .I4(demultiplexer_1_out2[3]), .I5(demultiplexer_1_out2[4]),
    .I6(demultiplexer_1_out2[5]), .I7(demultiplexer_1_out2[6]), .I8(demultiplexer_1_out2[7]),
    .O1(n8b_register_9_o1[0]), .O2(n8b_register_9_o1[1]), .O3(n8b_register_9_o1[2]),
    .O4(n8b_register_9_o1[3]), .O5(n8b_register_9_o1[4]), .O6(n8b_register_9_o1[5]),
    .O7(n8b_register_9_o1[6]), .O8(n8b_register_9_o1[7]), .En(demultiplexer_3_out2));
  _8b_Register u_8b_register_10 (
    .Inv(1'b0), .C(demultiplexer_2_out6), .I1(demultiplexer_1_out6[0]), .I2(demultiplexer_1_out6[1]),
    .I3(demultiplexer_1_out6[2]), .I4(demultiplexer_1_out6[3]), .I5(demultiplexer_1_out6[4]),
    .I6(demultiplexer_1_out6[5]), .I7(demultiplexer_1_out6[6]), .I8(demultiplexer_1_out6[7]),
    .O1(n8b_register_10_o1[0]), .O2(n8b_register_10_o1[1]), .O3(n8b_register_10_o1[2]),
    .O4(n8b_register_10_o1[3]), .O5(n8b_register_10_o1[4]), .O6(n8b_register_10_o1[5]),
    .O7(n8b_register_10_o1[6]), .O8(n8b_register_10_o1[7]), .En(demultiplexer_3_out6));
  _8b_Register u_8b_register_11 (
    .Inv(1'b0), .C(demultiplexer_2_out10), .I1(demultiplexer_1_out10[0]), .I2(demultiplexer_1_out10[1]),
    .I3(demultiplexer_1_out10[2]), .I4(demultiplexer_1_out10[3]), .I5(demultiplexer_1_out10[4]),
    .I6(demultiplexer_1_out10[5]), .I7(demultiplexer_1_out10[6]), .I8(demultiplexer_1_out10[7]),
    .O1(n8b_register_11_o1[0]), .O2(n8b_register_11_o1[1]), .O3(n8b_register_11_o1[2]),
    .O4(n8b_register_11_o1[3]), .O5(n8b_register_11_o1[4]), .O6(n8b_register_11_o1[5]),
    .O7(n8b_register_11_o1[6]), .O8(n8b_register_11_o1[7]), .En(demultiplexer_3_out10));
  _8b_Register u_8b_register_12 (
    .Inv(1'b0), .C(demultiplexer_2_out14), .I1(demultiplexer_1_out14[0]), .I2(demultiplexer_1_out14[1]),
    .I3(demultiplexer_1_out14[2]), .I4(demultiplexer_1_out14[3]), .I5(demultiplexer_1_out14[4]),
    .I6(demultiplexer_1_out14[5]), .I7(demultiplexer_1_out14[6]), .I8(demultiplexer_1_out14[7]),
    .O1(n8b_register_12_o1[0]), .O2(n8b_register_12_o1[1]), .O3(n8b_register_12_o1[2]),
    .O4(n8b_register_12_o1[3]), .O5(n8b_register_12_o1[4]), .O6(n8b_register_12_o1[5]),
    .O7(n8b_register_12_o1[6]), .O8(n8b_register_12_o1[7]), .En(demultiplexer_3_out14));
  _8b_Register u_8b_register_13 (
    .Inv(1'b0), .C(demultiplexer_2_out3), .I1(demultiplexer_1_out3[0]), .I2(demultiplexer_1_out3[1]),
    .I3(demultiplexer_1_out3[2]), .I4(demultiplexer_1_out3[3]), .I5(demultiplexer_1_out3[4]),
    .I6(demultiplexer_1_out3[5]), .I7(demultiplexer_1_out3[6]), .I8(demultiplexer_1_out3[7]),
    .O1(n8b_register_13_o1[0]), .O2(n8b_register_13_o1[1]), .O3(n8b_register_13_o1[2]),
    .O4(n8b_register_13_o1[3]), .O5(n8b_register_13_o1[4]), .O6(n8b_register_13_o1[5]),
    .O7(n8b_register_13_o1[6]), .O8(n8b_register_13_o1[7]), .En(demultiplexer_3_out3));
  _8b_Register u_8b_register_14 (
    .Inv(1'b0), .C(demultiplexer_2_out7), .I1(demultiplexer_1_out7[0]), .I2(demultiplexer_1_out7[1]),
    .I3(demultiplexer_1_out7[2]), .I4(demultiplexer_1_out7[3]), .I5(demultiplexer_1_out7[4]),
    .I6(demultiplexer_1_out7[5]), .I7(demultiplexer_1_out7[6]), .I8(demultiplexer_1_out7[7]),
    .O1(n8b_register_14_o1[0]), .O2(n8b_register_14_o1[1]), .O3(n8b_register_14_o1[2]),
    .O4(n8b_register_14_o1[3]), .O5(n8b_register_14_o1[4]), .O6(n8b_register_14_o1[5]),
    .O7(n8b_register_14_o1[6]), .O8(n8b_register_14_o1[7]), .En(demultiplexer_3_out7));
  _8b_Register u_8b_register_15 (
    .Inv(1'b0), .C(demultiplexer_2_out11), .I1(demultiplexer_1_out11[0]), .I2(demultiplexer_1_out11[1]),
    .I3(demultiplexer_1_out11[2]), .I4(demultiplexer_1_out11[3]), .I5(demultiplexer_1_out11[4]),
    .I6(demultiplexer_1_out11[5]), .I7(demultiplexer_1_out11[6]), .I8(demultiplexer_1_out11[7]),
    .O1(n8b_register_15_o1[0]), .O2(n8b_register_15_o1[1]), .O3(n8b_register_15_o1[2]),
    .O4(n8b_register_15_o1[3]), .O5(n8b_register_15_o1[4]), .O6(n8b_register_15_o1[5]),
    .O7(n8b_register_15_o1[6]), .O8(n8b_register_15_o1[7]), .En(demultiplexer_3_out11));
  _8b_Register u_8b_register_16 (
    .Inv(1'b0), .C(demultiplexer_2_out15), .I1(demultiplexer_1_out15[0]), .I2(demultiplexer_1_out15[1]),
    .I3(demultiplexer_1_out15[2]), .I4(demultiplexer_1_out15[3]), .I5(demultiplexer_1_out15[4]),
    .I6(demultiplexer_1_out15[5]), .I7(demultiplexer_1_out15[6]), .I8(demultiplexer_1_out15[7]),
    .O1(n8b_register_16_o1[0]), .O2(n8b_register_16_o1[1]), .O3(n8b_register_16_o1[2]),
    .O4(n8b_register_16_o1[3]), .O5(n8b_register_16_o1[4]), .O6(n8b_register_16_o1[5]),
    .O7(n8b_register_16_o1[6]), .O8(n8b_register_16_o1[7]), .En(demultiplexer_3_out15));
  Multiplexer #(.select(4), .width(8)) multiplexer_1 (
    .in0(n8b_register_1_o1), .in1(n8b_register_5_o1), .in2(n8b_register_9_o1), .in3(n8b_register_13_o1),
    .in4(n8b_register_2_o1), .in5(n8b_register_6_o1), .in6(n8b_register_10_o1), .in7(n8b_register_14_o1),
    .in8(n8b_register_3_o1), .in9(n8b_register_7_o1), .in10(n8b_register_11_o1), .in11(n8b_register_15_o1),
    .in12(n8b_register_4_o1), .in13(n8b_register_8_o1), .in14(n8b_register_12_o1), .in15(n8b_register_16_o1),
    .out({O7, O6, O5, O4, O3, O2, O1, O0}), .sel({R3, R2, R1, R0}), .en(En));

  // Notes on the sheet:
  //   DIn
  //   Clock
  //   Enable
  //   DOut
endmodule

module Register_Module (
  input  En,
  input  C,
  input  Set_I,
  input  Set_M,
  input  Set_IP,
  input  Set_MP,
  input  B0,
  input  B1,
  input  B2,
  input  B3,
  input  B4,
  input  IP_to_Bus,
  input  Mem_to_Bus,
  input  MP_to_Bus,
  input  B5,
  input  B6,
  input  B7,
  input  Instruction,
  input  [7:0] MP_In,
  input  MP_In_Switch,
  input  [7:0] IP_In,
  input  IP_In_Switch,
  input  [7:0] Mem_In,
  input  Mem_In_Switch,
  output O0,
  output O1,
  output O2,
  output O3,
  output O4,
  output O5,
  output O6,
  output O7,
  output In_to_Mem,
  output Mem_to_Out,
  output Stack_to_IP,
  output IP_to_Stack,
  output Dec_MP,
  output Inc_MP,
  output Dec_Mem,
  output Inc_Mem,
  output [7:0] MP_Out,
  output [7:0] IP_Out,
  output [7:0] Mem_Out
);

  wire demultiplexer_2_out0, demultiplexer_2_out1, demultiplexer_2_out2, demultiplexer_2_out3,
       demultiplexer_3_out0, demultiplexer_3_out1, demultiplexer_3_out2, demultiplexer_3_out3,
       demultiplexer_4_out8, or_1_out;
  wire [1:0] n2b_selector_1_o0, n2b_selector_2_o0;
  wire [3:0] Instruction_o1;
  wire [7:0] demultiplexer_1_out0, demultiplexer_1_out1, demultiplexer_1_out2, demultiplexer_1_out3,
       multiplexer_1_out, multiplexer_2_out, multiplexer_3_out;

  _2b_Selector u_2b_selector_1 (
    .S0(Set_I), .S1(Set_M), .S2(Set_IP), .S3(Set_MP), .O0(n2b_selector_1_o0[0]), .O1(n2b_selector_1_o0[1]));  // open: En
  Demultiplexer #(.select(2), .width(8)) demultiplexer_1 (
    .out0(demultiplexer_1_out0), .out1(demultiplexer_1_out1), .out2(demultiplexer_1_out2),
    .out3(demultiplexer_1_out3), .in({B7, B6, B5, B4, B3, B2, B1, B0}), .sel(n2b_selector_1_o0), .en(En));
  Demultiplexer #(.select(2)) demultiplexer_2 (
    .out0(demultiplexer_2_out0), .out1(demultiplexer_2_out1), .out2(demultiplexer_2_out2),
    .out3(demultiplexer_2_out3), .in(En), .sel(n2b_selector_1_o0), .en(En));
  Demultiplexer #(.select(2)) demultiplexer_3 (
    .out0(demultiplexer_3_out0), .out1(demultiplexer_3_out1), .out2(demultiplexer_3_out2),
    .out3(demultiplexer_3_out3), .in(C), .sel(n2b_selector_1_o0), .en(En));
  Demultiplexer #(.select(4), .enable("false")) demultiplexer_4 (
    .out0(Inc_Mem), .out1(Dec_Mem), .out2(Inc_MP), .out3(Dec_MP), .out4(IP_to_Stack), .out5(Stack_to_IP),
    .out6(Mem_to_Out), .out7(In_to_Mem), .out8(demultiplexer_4_out8), .out9(demultiplexer_4_out8),
    .out10(demultiplexer_4_out8), .out11(demultiplexer_4_out8), .out12(demultiplexer_4_out8),
    .out13(demultiplexer_4_out8), .out14(demultiplexer_4_out8), .out15(demultiplexer_4_out8),
    .in(Instruction), .sel(Instruction_o1));
  _4b_Register u_Instruction (
    .Inv(1'b0), .C(demultiplexer_3_out0), .I1(demultiplexer_1_out0[0]), .I2(demultiplexer_1_out0[1]),
    .I3(demultiplexer_1_out0[2]), .I4(demultiplexer_1_out0[3]), .O1(Instruction_o1[0]),
    .O2(Instruction_o1[1]), .O3(Instruction_o1[2]), .O4(Instruction_o1[3]), .En(demultiplexer_2_out0));
  _8b_Register Memory (
    .Inv(1'b0), .C(demultiplexer_3_out2), .I1(multiplexer_1_out[0]), .I2(multiplexer_1_out[1]),
    .I3(multiplexer_1_out[2]), .I4(multiplexer_1_out[3]), .I5(multiplexer_1_out[4]),
    .I6(multiplexer_1_out[5]), .I7(multiplexer_1_out[6]), .I8(multiplexer_1_out[7]), .O1(Mem_Out[0]),
    .O2(Mem_Out[1]), .O3(Mem_Out[2]), .O4(Mem_Out[3]), .O5(Mem_Out[4]), .O6(Mem_Out[5]), .O7(Mem_Out[6]),
    .O8(Mem_Out[7]), .En(demultiplexer_2_out2));
  Multiplexer #(.width(8), .enable("false")) multiplexer_1 (
    .in0(demultiplexer_1_out2), .in1(Mem_In), .out(multiplexer_1_out), .sel(Mem_In_Switch));
  Multiplexer #(.width(8), .enable("false")) multiplexer_2 (
    .in0(demultiplexer_1_out1), .in1(IP_In), .out(multiplexer_2_out), .sel(IP_In_Switch));
  Multiplexer #(.width(8), .enable("false")) multiplexer_3 (
    .in0(demultiplexer_1_out3), .in1(MP_In), .out(multiplexer_3_out), .sel(MP_In_Switch));
  _8b_Register Instruction_Pointer (
    .Inv(1'b0), .C(demultiplexer_3_out1), .I1(multiplexer_2_out[0]), .I2(multiplexer_2_out[1]),
    .I3(multiplexer_2_out[2]), .I4(multiplexer_2_out[3]), .I5(multiplexer_2_out[4]),
    .I6(multiplexer_2_out[5]), .I7(multiplexer_2_out[6]), .I8(multiplexer_2_out[7]), .O1(IP_Out[0]),
    .O2(IP_Out[1]), .O3(IP_Out[2]), .O4(IP_Out[3]), .O5(IP_Out[4]), .O6(IP_Out[5]), .O7(IP_Out[6]),
    .O8(IP_Out[7]), .En(demultiplexer_2_out1));
  _8b_Register Memory_Pointer (
    .Inv(1'b0), .C(demultiplexer_3_out3), .I1(multiplexer_3_out[0]), .I2(multiplexer_3_out[1]),
    .I3(multiplexer_3_out[2]), .I4(multiplexer_3_out[3]), .I5(multiplexer_3_out[4]),
    .I6(multiplexer_3_out[5]), .I7(multiplexer_3_out[6]), .I8(multiplexer_3_out[7]), .O1(MP_Out[0]),
    .O2(MP_Out[1]), .O3(MP_Out[2]), .O4(MP_Out[3]), .O5(MP_Out[4]), .O6(MP_Out[5]), .O7(MP_Out[6]),
    .O8(MP_Out[7]), .En(demultiplexer_2_out3));
  _2b_Selector u_2b_selector_2 (
    .S1(MP_to_Bus), .S2(Mem_to_Bus), .S3(IP_to_Bus), .O0(n2b_selector_2_o0[0]), .O1(n2b_selector_2_o0[1]));  // open: En, S0
  Multiplexer #(.select(2), .width(8)) multiplexer_4 (
    .in1(Mem_Out), .in2(MP_Out), .in3(IP_Out), .out({O7, O6, O5, O4, O3, O2, O1, O0}),
    .sel(n2b_selector_2_o0), .en(or_1_out));  // open: in0
  or or_1 (or_1_out, IP_to_Bus, Mem_to_Bus, MP_to_Bus);

  // Notes on the sheet:
  //   Instruction Logic
  //   <
  //   >
  //   -
  //   +
  //   MP In (Setter)
  //   MP Out
  //   Bus/Setter Switch
  //   IP In (Setter)
  //   IP Out
  //   Bus/Setter Switch
  //   Mem In (Setter)
  //   Mem Out
  //   Bus/Setter Switch
  //   Com
  //   Per.
  //   ]
  //   [
endmodule

module Clock_Stage (
  input  C,
  input  En,
  input  R,
  output [7:0] out_4
);

  wire decoder_1_out8, inc_dec_4b_1_o0, inc_dec_4b_1_o1, inc_dec_4b_1_o2, multiplexer_1_out,
       multiplexer_2_out, multiplexer_3_out;
  wire [3:0] n4b_register_1_o1;

  Inc_Dec_4b inc_dec_4b_1 (
    .En(1'b1), .I_D(1'b0), .I0(n4b_register_1_o1[0]), .I1(n4b_register_1_o1[1]), .I2(n4b_register_1_o1[2]),
    .I3(n4b_register_1_o1[3]), .O0(inc_dec_4b_1_o0), .O1(inc_dec_4b_1_o1), .O2(inc_dec_4b_1_o2));  // open: O3
  Multiplexer multiplexer_1 (.in0(inc_dec_4b_1_o0), .in1(1'b0), .out(multiplexer_1_out), .sel(R));  // open: en
  Multiplexer multiplexer_2 (.in0(inc_dec_4b_1_o1), .in1(1'b0), .out(multiplexer_2_out), .sel(R));  // open: en
  Multiplexer multiplexer_3 (.in0(inc_dec_4b_1_o2), .in1(1'b0), .out(multiplexer_3_out), .sel(R));  // open: en
  _4b_Register u_4b_register_1 (
    .Inv(1'b0), .C(C), .I1(multiplexer_1_out), .I2(multiplexer_2_out), .I3(multiplexer_3_out), .I4(1'b0),
    .O1(n4b_register_1_o1[0]), .O2(n4b_register_1_o1[1]), .O3(n4b_register_1_o1[2]),
    .O4(n4b_register_1_o1[3]), .En(En));
  Decoder #(.select(4)) decoder_1 (
    .out0(out_4[7]), .out1(out_4[6]), .out2(out_4[5]), .out3(out_4[4]), .out4(out_4[3]), .out5(out_4[2]),
    .out6(out_4[1]), .out7(out_4[0]), .out8(decoder_1_out8), .out9(decoder_1_out8), .out10(decoder_1_out8),
    .out11(decoder_1_out8), .out12(decoder_1_out8), .out13(decoder_1_out8), .out14(decoder_1_out8),
    .out15(decoder_1_out8), .sel(n4b_register_1_o1));  // open: en
endmodule

module RAM_Module (
  input  C,
  input  I0,
  input  I1,
  input  I2,
  input  I3,
  input  I4,
  input  I5,
  input  I6,
  input  I7,
  input  Set_Address_Reg,
  input  Bus____Write,
  input  Read____Bus,
  output O0,
  output O1,
  output O2,
  output O3,
  output O4,
  output O5,
  output O6,
  output O7
);

  wire or_1_out;
  wire [7:0] demultiplexer_1_out0, demultiplexer_1_out1, n8b_register_1_o1, n256b_memory_1_bus_out;

  Demultiplexer #(.width(8)) demultiplexer_1 (
    .out0(demultiplexer_1_out0), .out1(demultiplexer_1_out1), .in({I7, I6, I5, I4, I3, I2, I1, I0}),
    .sel(Set_Address_Reg));  // open: en
  or or_1 (or_1_out, Bus____Write, Read____Bus);
  _8b_Register u_8b_register_1 (
    .Inv(1'b0), .C(C), .I1(demultiplexer_1_out1[0]), .I2(demultiplexer_1_out1[1]),
    .I3(demultiplexer_1_out1[2]), .I4(demultiplexer_1_out1[3]), .I5(demultiplexer_1_out1[4]),
    .I6(demultiplexer_1_out1[5]), .I7(demultiplexer_1_out1[6]), .I8(demultiplexer_1_out1[7]),
    .O1(n8b_register_1_o1[0]), .O2(n8b_register_1_o1[1]), .O3(n8b_register_1_o1[2]),
    .O4(n8b_register_1_o1[3]), .O5(n8b_register_1_o1[4]), .O6(n8b_register_1_o1[5]),
    .O7(n8b_register_1_o1[6]), .O8(n8b_register_1_o1[7]), .En(Set_Address_Reg));
  _256B_Memory u_256b_memory_1 (
    .C(C), .WIn(demultiplexer_1_out0), .Address(n8b_register_1_o1), .En(or_1_out), .WEn(Bus____Write),
    .Bus_Out(n256b_memory_1_bus_out));
  Multiplexer #(.width(8)) multiplexer_1 (
    .in1(n256b_memory_1_bus_out), .out({O7, O6, O5, O4, O3, O2, O1, O0}), .sel(Read____Bus));  // open: in0, en

  // Notes on the sheet:
  //   BUS
  //   Write Address
endmodule

module Instruction_Module (
  input  C,
  input  [7:0] BIn,
  input  Bus__Reg,
  input  Reg__Bus,
  input  Write_Inst,
  input  [7:0] WIn,
  input  [7:0] WAddr,
  output [7:0] BOut
);

  wire or_1_out;
  wire [7:0] multiplexer_1_out, n8b_register_1_o1, n256b_memory_1_bus_out;

  _8b_Register u_8b_register_1 (
    .Inv(1'b0), .C(C), .I1(BIn[0]), .I2(BIn[1]), .I3(BIn[2]), .I4(BIn[3]), .I5(BIn[4]), .I6(BIn[5]),
    .I7(BIn[6]), .I8(BIn[7]), .O1(n8b_register_1_o1[0]), .O2(n8b_register_1_o1[1]),
    .O3(n8b_register_1_o1[2]), .O4(n8b_register_1_o1[3]), .O5(n8b_register_1_o1[4]),
    .O6(n8b_register_1_o1[5]), .O7(n8b_register_1_o1[6]), .O8(n8b_register_1_o1[7]), .En(Bus__Reg));
  Multiplexer #(.width(8)) multiplexer_1 (
    .in0(n8b_register_1_o1), .in1(WAddr), .out(multiplexer_1_out), .sel(Write_Inst));  // open: en
  or or_1 (or_1_out, Reg__Bus, Write_Inst);
  _256B_Memory u_256b_memory_1 (
    .C(C), .WIn(WIn), .Address(multiplexer_1_out), .En(or_1_out), .WEn(Write_Inst),
    .Bus_Out(n256b_memory_1_bus_out));
  Multiplexer #(.width(8)) multiplexer_2 (.in1(n256b_memory_1_bus_out), .out(BOut), .sel(Reg__Bus));  // open: in0, en
endmodule
